# Fritzing sketch LCD_128x64_Arduino (saved by Fritzing 0.9.6b)
breadboards: 1

parts:
  GLCD_128x1 = 128 x 64 Graphic LCD
  Componente1 = Arduino Nano (Rev3.0)
  R1 = Resistor [tolerance=±5% resistance=100 package="0805 [SMD]"]
  R2 = TRIMPOT [package=3386u]
  VCC1 = 4 x AAA Battery Mount
  C1 = Electrolytic Capacitor [capacitance=10µF voltage=16V package="100 mil [THT, electrolytic]"]

nets:
  N1: GLCD_128x1.1_Vss, GLCD_128x1.15_CS1, GLCD_128x1.20_K(-), Componente1.GND, VCC1.-, C1.-
  N2: GLCD_128x1.2_Vdd, Componente1.5V, R2.CCW, R2.CW, C1.+
  N3: GLCD_128x1.3_Vo, R2.WIPER
  N4: GLCD_128x1.4_D/I, Componente1.D11/MOSI
  N5: GLCD_128x1.5_R/W, Componente1.D10
  N6: GLCD_128x1.6_Enable, Componente1.D13/SCK
  N7: GLCD_128x1.19_A(+), R1.Pin_0
  N8: Componente1.D4, R1.Pin_1

// code stored in the sketch: Untitled.ino

